// Logisim project 2024课设2_MultipleCycleMipsCpu.circ as structural Verilog: 7 circuits, main circuit L5硬布线控制器
module \L6单总线CPU_3级时序  (
  output [21:0] \控制总线 
);

  wire and_1_out, CLK, comparator_1_eq, equal, Mcal, Mex, Mif, Mint, mips_alu_1_equal, not_1_out, RST, T1,
       T2, T3, T4;
  wire [4:0] registerfile_1_p4, registerfile_1_p5;
  wire [11:0] Clks, \指令数 ;
  wire [31:0] AR_q, bit_extender_1_out, controlled_buffer_1_out, controlled_buffer_2_out, DR_q, IR,
       mips_alu_1_result, PC_q, ram_1_data, registerfile_1_p6, shifter_1_out, X_q, Z_q, \内部总线 ;

  LED #(.active("true")) led_1 (.in(Mcal));
  LED #(.active("true")) led_2 (.in(Mif));
  // Probe on Clks
  Register #(.width(32), .trigger("rising"), .Select("low")) AR (
    .D(\内部总线 ), .en(\控制总线 [13]), .Q(AR_q), .clk(CLK));  // open: clr
  // Digital_Oscilloscope #(.nState(35), .frontlines("rising"), .showclock("true")) digital_oscilloscope_1: pin names not known; wires that end beside it: CLK, Mif, Mcal, Mex, T1, T2, T3, T4, \控制总线 [2]
  LED #(.active("true")) led_3 (.in(T1));
  LED #(.active("true")) led_4 (.in(Mex));
  LED #(.active("true")) led_5 (.in(Mint));
  // Mips_Probe mips_probe_1: pin names not known; wires that end beside it: IR
  // Probe on controlled_buffer_1_out
  Register #(.width(32), .trigger("rising"), .Select("low")) X (
    .D(\内部总线 ), .en(\控制总线 [10]), .Q(X_q), .clk(CLK));  // open: clr
  LED #(.active("true")) led_6 (.in(T2));
  LED #(.active("true")) led_7 (.in(T3));
  // Probe on \指令数 
  LED #(.active("true")) led_8 (.in(T4));
  RAM #(.addrWidth(10), .dataWidth(32), .bus("separate"), .Select("high")) ram_1 (
    .addr(AR_q[11:2]), .din(controlled_buffer_1_out), .data(ram_1_data), .str(\控制总线 [0]), .clk(CLK),
    .ld(\控制总线 [1]));  // open: sel, clr
  assign controlled_buffer_1_out = \控制总线 [15] ? DR_q : 32'bz;  // Controlled_Buffer controlled_buffer_1
  MIPS_ALU mips_alu_1 (
    .X(X_q), .Y(\内部总线 ), .Equal(mips_alu_1_equal), .Result(mips_alu_1_result), .ADD(\控制总线 [4]),
    .ADD4(\控制总线 [3]), .SLT(\控制总线 [2]));  // open: SUB
  assign controlled_buffer_2_out = \控制总线 [11] ? \内部总线  : 32'bz;  // Controlled_Buffer controlled_buffer_2
  assign controlled_buffer_2_out = \控制总线 [12] ? ram_1_data : 32'bz;  // Controlled_Buffer controlled_buffer_3
  // Probe on \内部总线 
  Register #(.width(32), .trigger("rising"), .Select("low")) PC (
    .D(\内部总线 ), .en(\控制总线 [14]), .Q(PC_q), .clk(CLK), .clr(RST));
  assign \内部总线  = \控制总线 [21] ? PC_q : 32'bz;  // Controlled_Buffer controlled_buffer_4
  assign \内部总线  = \控制总线 [20] ? DR_q : 32'bz;  // Controlled_Buffer controlled_buffer_5
  Register #(.width(32), .trigger("rising"), .Select("low")) DR (
    .D(controlled_buffer_2_out), .Q(DR_q), .clk(CLK));  // open: en, clr
  Register #(.width(1), .trigger("rising"), .Select("low")) PSW (
    .D(mips_alu_1_equal), .en(\控制总线 [7]), .Q(equal), .clk(CLK));  // open: clr
  Register #(.width(32), .trigger("rising"), .Select("low")) Z (
    .D(mips_alu_1_result), .Q(Z_q), .clk(CLK));  // open: en, clr
  assign \内部总线  = \控制总线 [19] ? Z_q : 32'bz;  // Controlled_Buffer controlled_buffer_6
  Register #(.width(32), .trigger("rising"), .Select("low")) u_IR (
    .D(\内部总线 ), .en(\控制总线 [8]), .Q(IR), .clk(CLK));  // open: clr
  assign \内部总线  = \控制总线 [17] ? bit_extender_1_out : 32'bz;  // Controlled_Buffer controlled_buffer_7
  assign \内部总线  = \控制总线 [16] ? shifter_1_out : 32'bz;  // Controlled_Buffer controlled_buffer_8
  \L5硬布线控制器  \l5硬布线控制器_1  (
    .\状态节拍信号 ({T4, T3, T2, T1, Mex, Mcal, Mif}), .CLK(CLK), .IR(IR), .ControlBus(\控制总线 ), .EQUAL(equal));
  // RegisterFile registerfile_1: pin names not known; wires that end beside it: \内部总线 , CLK, \控制总线 [9], registerfile_1_p4, registerfile_1_p5, registerfile_1_p6
  assign bit_extender_1_out = {{16{IR[15]}}, IR[15:0]};  // Bit_Extender bit_extender_1
  assign \内部总线  = \控制总线 [18] ? registerfile_1_p6 : 32'bz;  // Controlled_Buffer controlled_buffer_9
  Multiplexer #(.select(1), .width(5), .disabled("Z"), .enable("false")) multiplexer_1 (
    .in0(IR[25:21]), .in1(IR[20:16]), .out(registerfile_1_p5), .sel(\控制总线 [6]));
  Multiplexer #(.select(1), .width(5), .disabled("Z"), .enable("false")) multiplexer_2 (
    .in0(IR[20:16]), .in1(IR[15:11]), .out(registerfile_1_p4), .sel(\控制总线 [5]));
  Comparator #(.width(32), .mode("twosComplement")) comparator_1 (
    .a(IR), .b(32'h1000ffff), .eq(comparator_1_eq));  // open: gt, lt
  not not_1 (not_1_out, comparator_1_eq);
  Clock #(.highDuration(1), .lowDuration(1)) clock_1 (.out(CLK));
  Shifter #(.width(32), .shift("ll")) shifter_1 (.in(bit_extender_1_out), .\dist (5'b00010), .out(shifter_1_out));
  Counter #(.width(12), .max('hfff), .ongoal("wrap"), .trigger("falling"), .behavior("new")) counter_1 (
    .count(not_1_out), .Q(Clks), .clk(CLK));  // open: load, D, carry, clr, preset, down
  and and_1 (and_1_out, not_1_out, Mif, T1);
  Counter #(.width(12), .max('hfff), .ongoal("wrap"), .trigger("falling"), .behavior("old")) counter_2 (
    .count(and_1_out), .Q(\指令数 ), .clk(CLK));  // open: load, D, carry, clr, preset

  // Other names for the same wires on the sheet: rd[4:0] = IR[15:11]; rt[4:0] = IR[20:16]; rs[4:0] = IR[25:21];
  //   Write = \控制总线 [0]; READ = \控制总线 [1]; Slt = \控制总线 [2]; Add4 = \控制总线 [3]; Add = \控制总线 [4]; RegDst = \控制总线 [5];
  //   RegTgt = \控制总线 [6]; PSWin = \控制总线 [7]; IRin = \控制总线 [8]; Rin = \控制总线 [9]; Xin = \控制总线 [10]; DRin = \控制总线 [11];
  //   DREin = \控制总线 [12]; ARin = \控制总线 [13]; PCin = \控制总线 [14]; DREout = \控制总线 [15]; IR_A_out = \控制总线 [16];
  //   IR_I_out = \控制总线 [17]; Rout = \控制总线 [18]; Zout = \控制总线 [19]; DRout = \控制总线 [20]; PCout = \控制总线 [21];
  //   状态节拍信号[6:0] = {T4, T3, T2, T1, Mex, Mcal, Mif}

  // Notes on the sheet:
  //   单总线结构 MIPS CPU
  //   MEM
  //   外部总线
  //   内部总线
  //   三级时序
  //   Immediate32
  //   AddressOffset32
endmodule

// 硬布线
module \L5硬布线控制器  (
  input  CLK,
  input  [31:0] IR,
  input  EQUAL,
  output [6:0] \状态节拍信号 ,
  output [21:0] ControlBus
);

  wire ADDI, BEQ, LW, Other;
  wire [3:0] \l2时序发生器状态机_定长指令周期_1_n0 , register_1_q;
  wire [12:9] OCInput;

  Register #(.width(4), .trigger("falling"), .Select("low")) register_1 (
    .D(\l2时序发生器状态机_定长指令周期_1_n0 ), .Q(register_1_q), .clk(CLK));  // open: en, clr
  \L2时序发生器状态机_定长指令周期  \l2时序发生器状态机_定长指令周期_1  (
    .S3(register_1_q[3]), .S2(register_1_q[2]), .S1(register_1_q[1]), .S0(register_1_q[0]),
    .N3(\l2时序发生器状态机_定长指令周期_1_n0 [3]), .N2(\l2时序发生器状态机_定长指令周期_1_n0 [2]), .N1(\l2时序发生器状态机_定长指令周期_1_n0 [1]),
    .N0(\l2时序发生器状态机_定长指令周期_1_n0 [0]));
  \L3时序发生器输出函数_定长指令周期  \l3时序发生器输出函数_定长指令周期_1  (
    .S3(register_1_q[3]), .S2(register_1_q[2]), .S1(register_1_q[1]), .S0(register_1_q[0]),
    .Mif(\状态节拍信号 [0]), .Mcal(\状态节拍信号 [1]), .Mex(\状态节拍信号 [2]), .T1(\状态节拍信号 [3]), .T2(\状态节拍信号 [4]),
    .T3(\状态节拍信号 [5]), .T4(\状态节拍信号 [6]));
  \L1指令译码器  \l1指令译码器_1  (
    .IR(IR), .LW(LW), .SW(OCInput[9]), .BEQ(BEQ), .ADDI(ADDI), .SLT(OCInput[12]), .OtherInstr(Other));
  \L4硬布线控制器组合逻辑单元  \l4硬布线控制器组合逻辑单元_1  (
    .SLT(OCInput[12]), .ADDI(ADDI), .LW(LW), .SW(OCInput[9]), .BEQ(BEQ), .Mif(\状态节拍信号 [0]),
    .Mcal(\状态节拍信号 [1]), .Mex(\状态节拍信号 [2]), .T1(\状态节拍信号 [3]), .T2(\状态节拍信号 [4]), .T3(\状态节拍信号 [5]),
    .T4(\状态节拍信号 [6]), .EQUAL(EQUAL), .Pcout(ControlBus[21]), .DRout(ControlBus[20]), .Zout(ControlBus[19]),
    .Rout(ControlBus[18]), .IRiout(ControlBus[17]), .IRaout(ControlBus[16]), .DREout(ControlBus[15]),
    .Pcin(ControlBus[14]), .ARin(ControlBus[13]), .DREin(ControlBus[12]), .DRin(ControlBus[11]),
    .Xin(ControlBus[10]), .Rin(ControlBus[9]), .IRin(ControlBus[8]), .PSWin(ControlBus[7]),
    .RegTgt(ControlBus[6]), .RegDst(ControlBus[5]), .Add(ControlBus[4]), .Add4(ControlBus[3]),
    .Slt_2(ControlBus[2]), .READ(ControlBus[1]), .WRITE(ControlBus[0]));

  // Other names for the same wires on the sheet: Write = ControlBus[0]; READ = ControlBus[1]; Slt_t = ControlBus[2];
  //   Add4 = ControlBus[3]; Add = ControlBus[4]; RegDst = ControlBus[5]; RegTgt = ControlBus[6];
  //   PSWin = ControlBus[7]; IRin = ControlBus[8]; Rin = ControlBus[9]; Xin = ControlBus[10]; DRin = ControlBus[11];
  //   DREin = ControlBus[12]; ARin = ControlBus[13]; PCin = ControlBus[14]; DREout = ControlBus[15];
  //   IR_A_out = ControlBus[16]; IR_I_out = ControlBus[17]; Rout = ControlBus[18]; Zout = ControlBus[19];
  //   DRout = ControlBus[20]; PCout = ControlBus[21];
  //   OCInput (some bits) = {ADDI, LW, BEQ, \状态节拍信号 [0], \状态节拍信号 [1], \状态节拍信号 [2], \状态节拍信号 [3], \状态节拍信号 [4], \状态节拍信号 [5], \状态节拍信号 [6], EQUAL};
  //   T4 = \状态节拍信号 [6]; T3 = \状态节拍信号 [5]; T2 = \状态节拍信号 [4]; T1 = \状态节拍信号 [3]; Mex = \状态节拍信号 [2]; Mcal = \状态节拍信号 [1];
  //   Mif = \状态节拍信号 [0]; SW = OCInput[9]; SLT = OCInput[12]; 指令字[31:0] = IR

  // Notes on the sheet:
  //   不要改变此引脚区域内容，也不要改变封装形式
  //   指令译码信号
  //   状态寄存器
  //   状态寄存器应该下跳沿？
  //   现态
  //   FSM状态机
  //   次态
  //   状态机
  //   输出函数
  //   输入输出引脚
  //   时序发生器TG
  //   指令译码器
  //   如发现控制信号有错可以直接查看具体哪位信号出错
  //   指令译码信号
  //   指令译码逻辑ID
  //   硬布线控制器组合逻辑单元
endmodule

// Decoder
module \L1指令译码器  (
  input  [31:0] IR,
  output LW,
  output SW,
  output BEQ,
  output ADDI,
  output SLT,
  output OtherInstr
);

  wire comparator_5_eq, comparator_6_eq;

  Comparator #(.width(6), .mode("twosComplement")) comparator_1 (
    .a(IR[31:26]), .b(6'b100011), .eq(LW));  // open: gt, lt
  Comparator #(.width(6), .mode("twosComplement")) comparator_2 (
    .a(IR[31:26]), .b(6'b101011), .eq(SW));  // open: gt, lt
  Comparator #(.width(6), .mode("twosComplement")) comparator_3 (
    .a(IR[31:26]), .b(6'b000100), .eq(BEQ));  // open: gt, lt
  Comparator #(.width(6), .mode("twosComplement")) comparator_4 (
    .a(IR[31:26]), .b(6'b001000), .eq(ADDI));  // open: gt, lt
  Comparator #(.width(6), .mode("twosComplement")) comparator_5 (
    .a(IR[5:0]), .b(6'b101010), .eq(comparator_5_eq));  // open: gt, lt
  Comparator #(.width(6), .mode("twosComplement")) comparator_6 (
    .a(IR[31:26]), .b({6{1'b0}}), .eq(comparator_6_eq));  // open: gt, lt
  and and_1 (SLT, comparator_5_eq, comparator_6_eq);
  nor nor_1 (OtherInstr, BEQ, SW, LW, ADDI, SLT);

  // Other names for the same wires on the sheet: FUNCT[5:0] = IR[5:0]; OP[5:0] = IR[31:26]

  // Notes on the sheet:
  //   请勿增删改引脚，否则可能引起子电路外观变化，无法自动测试
  //   常用常量
  //   将指令字IR转换成指令译码信息，每一个输出代表一条不同的指令
endmodule

// 状态机
module \L2时序发生器状态机_定长指令周期  (
  input  S3,
  input  S2,
  input  S1,
  input  S0,
  output N3,
  output N2,
  output N1,
  output N0
);

  wire and_1_out, and_2_out, and_3_out, and_4_out, and_5_out, and_6_out, and_7_out, and_8_out, not_1_out,
       not_2_out, not_3_out, not_4_out, not_5_out, not_6_out, not_7_out, not_8_out;

  and and_1 (and_1_out, S2, S1, S0);
  and and_2 (and_2_out, S3, not_1_out);
  not not_1 (not_1_out, S1);
  and and_3 (and_3_out, S3, not_2_out);
  not not_2 (not_2_out, S0);
  not not_3 (not_3_out, S3);
  not not_4 (not_4_out, S2);
  not not_5 (not_5_out, S1);
  not not_6 (not_6_out, S0);
  not not_7 (not_7_out, S1);
  and and_4 (and_4_out, not_7_out, S0);
  and and_5 (and_5_out, S1, not_8_out);
  not not_8 (not_8_out, S0);
  not not_9 (N0, S0);
  or or_1 (N3, and_1_out, and_2_out, and_3_out);
  and and_6 (and_6_out, not_3_out, not_4_out, S1, S0);
  and and_7 (and_7_out, S2, not_5_out);
  or or_2 (N2, and_6_out, and_7_out, and_8_out);
  and and_8 (and_8_out, S2, not_6_out);
  or or_3 (N1, and_4_out, and_5_out);
endmodule

// 输出函数
module \L3时序发生器输出函数_定长指令周期  (
  input  S3,
  input  S2,
  input  S1,
  input  S0,
  output Mif,
  output Mcal,
  output Mex,
  output T1,
  output T2,
  output T3,
  output T4
);

  wire not_1_out, not_2_out, not_3_out, not_4_out, not_5_out, not_6_out;

  not not_1 (not_1_out, S3);
  and and_1 (Mif, not_1_out, not_2_out);
  not not_2 (not_2_out, S2);
  not not_3 (not_3_out, S1);
  and and_2 (T1, not_3_out, not_4_out);
  not not_4 (not_4_out, S0);
  not not_5 (not_5_out, S1);
  and and_3 (T2, not_5_out, S0);
  and and_4 (T3, S1, not_6_out);
  not not_6 (not_6_out, S0);
  and and_5 (T4, S1, S0);

  assign Mcal = S2;
  assign Mex = S3;
endmodule

// 硬布线控制器组合逻辑单元
module \L4硬布线控制器组合逻辑单元  (
  input  SLT,
  input  ADDI,
  input  LW,
  input  SW,
  input  BEQ,
  input  Mif,
  input  Mcal,
  input  Mex,
  input  T1,
  input  T2,
  input  T3,
  input  T4,
  input  EQUAL,
  output Pcout,
  output DRout,
  output Zout,
  output Rout,
  output IRiout,
  output IRaout,
  output DREout,
  output Pcin,
  output ARin,
  output DREin,
  output DRin,
  output Xin,
  output Rin,
  output IRin,
  output PSWin,
  output RegTgt,
  output RegDst,
  output Add,
  output Add4,
  output Slt_2,
  output READ,
  output WRITE
);

  wire and_1_out, and_2_out, and_3_out, and_4_out, and_5_out, and_6_out, and_7_out, and_8_out, and_9_out,
       and_10_out, and_11_out, and_12_out, and_13_out, and_14_out, and_15_out, and_16_out, and_17_out,
       and_18_out, and_19_out, and_20_out, and_21_out, and_24_out, and_25_out, and_26_out, and_27_out,
       and_28_out, and_29_out, and_30_out, and_32_out, and_33_out, and_34_out, and_35_out, and_36_out,
       and_37_out, and_38_out, and_39_out, and_40_out, and_41_out, and_44_out, and_45_out, and_46_out,
       and_48_out, and_49_out, and_50_out, and_51_out, and_54_out, and_55_out;

  and and_1 (and_1_out, Mif, T1);
  and and_2 (and_2_out, BEQ, Mex, T1);
  and and_3 (and_3_out, Mif, T4);
  and and_4 (and_4_out, LW, Mex, T3);
  and and_5 (and_5_out, Mif, T3);
  and and_6 (and_6_out, BEQ, Mex, T3, EQUAL);
  and and_7 (and_7_out, SW, Mex, T1);
  and and_8 (and_8_out, LW, Mex, T1);
  and and_9 (and_9_out, ADDI, Mex, T3);
  and and_10 (and_10_out, SLT, Mex, T3);
  and and_11 (and_11_out, BEQ, Mcal, T2);
  and and_12 (and_12_out, BEQ, Mcal, T1);
  and and_13 (and_13_out, SW, Mex, T2);
  and and_14 (and_14_out, SW, Mcal, T1);
  and and_15 (and_15_out, LW, Mcal, T1);
  and and_16 (and_16_out, ADDI, Mex, T1);
  and and_17 (and_17_out, SLT, Mex, T2);
  and and_18 (and_18_out, SLT, Mex, T1);
  and and_19 (and_19_out, SW, Mcal, T2);
  and and_20 (and_20_out, LW, Mcal, T2);
  and and_21 (and_21_out, ADDI, Mex, T2);
  and and_22 (IRaout, BEQ, Mex, T2);
  and and_23 (DREout, SW, Mex, T3);
  and and_24 (and_24_out, Mif, T3);
  and and_25 (and_25_out, BEQ, Mex, T3, EQUAL);
  and and_26 (and_26_out, Mif, T1);
  and and_27 (and_27_out, SW, Mex, T1);
  and and_28 (and_28_out, LW, Mex, T1);
  and and_29 (and_29_out, Mif, T3);
  and and_30 (and_30_out, LW, Mex, T2);
  and and_31 (DRin, SW, Mex, T2);
  and and_32 (and_32_out, Mif, T1);
  and and_33 (and_33_out, BEQ, Mex, T1);
  and and_34 (and_34_out, BEQ, Mcal, T1);
  and and_35 (and_35_out, SW, Mcal, T1);
  and and_36 (and_36_out, LW, Mcal, T1);
  and and_37 (and_37_out, ADDI, Mex, T1);
  and and_38 (and_38_out, SLT, Mex, T1);
  and and_39 (and_39_out, LW, Mex, T3);
  and and_40 (and_40_out, ADDI, Mex, T3);
  and and_41 (and_41_out, SLT, Mex, T3);
  and and_42 (IRin, Mif, T4);
  and and_43 (PSWin, BEQ, Mcal, T2);
  and and_44 (and_44_out, BEQ, Mcal, T2);
  and and_45 (and_45_out, SW, Mex, T2);
  and and_46 (and_46_out, SLT, Mex, T2);
  and and_47 (RegDst, SLT, Mex, T3);
  and and_48 (and_48_out, BEQ, Mex, T2);
  and and_49 (and_49_out, SW, Mcal, T2);
  and and_50 (and_50_out, LW, Mcal, T2);
  and and_51 (and_51_out, ADDI, Mex, T2);
  and and_52 (Add4, Mif, T2);
  and and_53 (Slt_2, SLT, Mex, T2);
  and and_54 (and_54_out, Mif, T3);
  and and_55 (and_55_out, LW, Mex, T2);
  and and_56 (WRITE, SW, Mex, T3);
  or or_1 (Pcout, and_1_out, and_2_out);
  or or_2 (DRout, and_3_out, and_4_out);
  or or_3 (Zout, and_5_out, and_6_out, and_7_out, and_8_out, and_9_out, and_10_out);
  or or_4 (Rout, and_11_out, and_12_out, and_13_out, and_14_out, and_15_out, and_16_out, and_17_out, and_18_out);
  or or_5 (IRiout, and_19_out, and_20_out, and_21_out);
  or or_6 (Pcin, and_24_out, and_25_out);
  or or_7 (ARin, and_26_out, and_27_out, and_28_out);
  or or_8 (DREin, and_29_out, and_30_out);
  or or_9 (Xin, and_32_out, and_33_out, and_34_out, and_35_out, and_36_out, and_37_out, and_38_out);
  or or_10 (Rin, and_39_out, and_40_out, and_41_out);
  or or_11 (RegTgt, and_44_out, and_45_out, and_46_out);
  or or_12 (Add, and_48_out, and_49_out, and_50_out, and_51_out);
  or or_13 (READ, and_54_out, and_55_out);
endmodule

// ALU
module MIPS_ALU (
  input  ADD,
  input  ADD4,
  input  [31:0] X,
  input  [31:0] Y,
  input  SUB,
  input  SLT,
  output Equal,
  output [31:0] Result
);

  wire [0:0] comparator_1_lt;
  wire [1:0] priority_encoder_1_out;
  wire [31:0] adder_1_out, adder_2_out, subtractor_1_out;

  Pull_Resistor #(.pull(0)) pull_resistor_1 (.node(Y));
  Adder #(.width(32)) adder_1 (.a(X), .b(Y), .out(adder_1_out));  // open: cin, cout
  Adder #(.width(32)) adder_2 (.a(X), .b(32'h4), .out(adder_2_out));  // open: cin, cout
  Subtractor #(.width(32)) subtractor_1 (.a(X), .b(Y), .out(subtractor_1_out));  // open: bin, bout
  Comparator #(.width(32), .mode("twosComplement")) comparator_1 (
    .a(X), .b(Y), .eq(Equal), .lt(comparator_1_lt[0]));  // open: gt
  Priority_Encoder #(.select(2), .disabled("Z")) priority_encoder_1 (
    .in0(ADD), .in1(ADD4), .in2(SUB), .in3(SLT), .out(priority_encoder_1_out));  // open: gs, en_out, en_in
  Pull_Resistor #(.pull(0)) pull_resistor_2 (.node(priority_encoder_1_out));
  Multiplexer #(.select(2), .width(32), .disabled("Z"), .enable("false")) multiplexer_1 (
    .in0(adder_1_out), .in1(adder_2_out), .in2(subtractor_1_out), .in3({{31{1'b0}}, comparator_1_lt[0]}),
    .out(Result), .sel(priority_encoder_1_out));

  // Notes on the sheet:
  //   不要改变此引脚区域内容，也不要改变ALU封装形式
  //   输入引脚
  //   输出引脚
endmodule
